# Fritzing sketch schematic BMW interior light control (saved by Fritzing 0.9.3b)
circuit board: 2.8cm x 2.3cm
breadboards: 1

parts:
  R1 = Resistor [tolerance=±5% resistance=1k part_number=1k package=THT]
  R2 = Resistor [tolerance=±5% resistance=10k part_number=10k package=THT]
  R3 = Resistor [tolerance=±5% resistance=100k part_number=100k package=THT]
  Q1 = Basic FET N-Channel [part_number=IRFZ44N package="TO220 [THT]"]
  J1 = male pin header, 8 pins [form="♂ (male)"]
  Digispark1 = Digispark [part_number=Digispark]
  R6 = TRIMPOT [part_number=10k package=trim_pot_pth]
  SIP-1A05 = female pin header, 4 pins [form="♀ (female)" part_number=SIP-1A05]

nets:
  N1: R1.Pin_0, J1.pin5, Digispark1.VCC, R6.CW
  N2: R1.Pin_1, J1.pin3, Digispark1.P1
  N3: R2.Pin_0, J1.pin4, Digispark1.P2
  N4: R2.Pin_1, R3.Pin_1, Q1.source, J1.pin8, Digispark1.GND, R6.CCW, SIP-1A05.pin1, SIP-1A05.pin2
  N5: R3.Pin_0, Q1.gate, Digispark1.P0
  N6: Q1.drain, J1.pin2
  N7: J1.pin1, Digispark1.VIN
  N8: J1.pin6, SIP-1A05.pin3
  N9: J1.pin7, SIP-1A05.pin4
  N10: Digispark1.P4, R6.WIPER

notes:
  12v
  L-Out
  L-In
  Sens-
  Sens+
  Unlock+
  Door-
  Gnd
  Interior Light
  Controller
  Designed By Raku
  For E30/E32/E34/E36

custom parts:
  Digispark: The Digispark is an Attiny85 based microcontroller development board similar to the Arduino line, only cheaper, smaller, and a bit less powerful. With a whole host of shields to extend its functionality and the ability to use the familiar Arduino IDE the Digispark is a great way to jump into electronics, or perfect for when an Arduino is too big or too much.
